# Fritzing sketch RTCcheckV06 (saved by Fritzing 1.0.5)
circuit board: 13.5123cm x 6.48408cm
breadboards: 1

parts:
  TCA9548A = Adafruit TCA9548A
  SK6812/WS2812 = SMD RGB LED (SK6812) [package=5050]
  Arduino_Nano = Arduino NANO RP2040 CONNECT with headers
  RTC-0 = female pin header, 6 pins [form="♀ (female)"]
  RTC-1 = female pin header, 6 pins [form="♀ (female)"]
  RTC-2 = female pin header, 6 pins [form="♀ (female)"]
  RTC-3 = female pin header, 6 pins [form="♀ (female)"]
  RTC-4 = female pin header, 6 pins [form="♀ (female)"]
  RTC-5 = female pin header, 6 pins [form="♀ (female)"]
  RTC-6 = female pin header, 6 pins [form="♀ (female)"]
  RTC-7 = female pin header, 6 pins [form="♀ (female)"]
  LED = female pin header, 3 pins [form="♀ (female)"]
  POWER = screw terminal, 2 pins
  C2 = Electrolytic Capacitor [capacitance=10µF voltage=35V package="100 mil [THT, electrolytic]"]
  1N5818 = Rectifier Diode [part_number=1N4001 package="300 mil [THT]"]
  1000_uF1 = Electrolytic Capacitor [capacitance=1mF voltage=16V package="100 mil [THT, electrolytic]"]
  RTCclock10 = female pin header, 15 pins [form="♀ (female)"]
  RTCclock11 = female pin header, 15 pins [form="♀ (female)"]
  R16 = Resistor [tolerance=±5% resistance=10k power=0.25W package=THT]
  LDR1 = male pin header, 2 pins [form="♂ (male)"]
  RTCclock12 = female pin header, 12 pins [form="♀ (female)"]
  SQW_32K-0 = male pin header, 2 pins [form="♂ (male)"]
  SQW_32K-1 = male pin header, 2 pins [form="♂ (male)"]
  SQW_32K-2 = male pin header, 2 pins [form="♂ (male)"]
  SQW_32K-3 = male pin header, 2 pins [form="♂ (male)"]
  SQW_32K-5 = male pin header, 2 pins [form="♂ (male)"]
  SQW_32K-4 = male pin header, 2 pins [form="♂ (male)"]
  SQW_32K6 = male pin header, 2 pins [form="♂ (male)"]
  SQW_32K7 = male pin header, 2 pins [form="♂ (male)"]

nets:
  N1: TCA9548A.2SDA, RTC-2.pin3
  N2: TCA9548A.2SCL, RTC-2.pin4
  N3: TCA9548A.3SDA, RTC-3.pin3
  N4: TCA9548A.3SCL, RTC-3.pin4
  N5: TCA9548A.4SDA, RTC-4.pin3
  N6: TCA9548A.4SCL, RTC-4.pin4
  N7: TCA9548A.5SDA, RTC-5.pin3
  N8: TCA9548A.5SCL, RTC-5.pin4
  N9: TCA9548A.6SDA, RTC-6.pin3
  N10: TCA9548A.6SCL, RTC-6.pin4
  N11: TCA9548A.7SDA, RTC-7.pin3
  N12: TCA9548A.7SCL, RTC-7.pin4
  VCC: TCA9548A.VCC, Arduino_Nano.+3V3, RTC-0.pin2, RTC-1.pin2, RTC-2.pin2, RTC-3.pin2, RTC-4.pin2, RTC-5.pin2, RTC-6.pin2, RTC-7.pin2, C2.+, RTCclock11.pin14, LDR1.pin2, RTCclock12.pin1
  GND: TCA9548A.GND, SK6812/WS2812.GND, Arduino_Nano.GND-4, Arduino_Nano.GND-29, RTC-0.pin1, RTC-1.pin1, RTC-2.pin1, RTC-3.pin1, RTC-4.pin1, RTC-5.pin1, RTC-6.pin1, RTC-7.pin1, LED.pin1, POWER.pin1, C2.-, 1000_uF1.-, RTCclock10.pin4, RTCclock11.pin2, R16.Pin_0, RTCclock12.pin2
  N13: TCA9548A.INPUTSDA, Arduino_Nano.D18, RTCclock11.pin8, RTCclock12.pin3
  N14: TCA9548A.INPUTSCL, Arduino_Nano.D19, RTCclock11.pin7, RTCclock12.pin4
  N15: TCA9548A.RESET, RTCclock12.pin5
  N16: TCA9548A.A0, RTCclock12.pin6
  N17: TCA9548A.A1, RTCclock12.pin7
  N18: TCA9548A.A2, RTCclock12.pin8
  N19: TCA9548A.0SDA, RTC-0.pin3, RTCclock12.pin9
  N20: TCA9548A.0SCL, RTC-0.pin4, RTCclock12.pin10
  N21: TCA9548A.1SDA, RTC-1.pin3, RTCclock12.pin11
  N22: TCA9548A.1SCL, RTC-1.pin4, RTCclock12.pin12
  VCC_2: SK6812/WS2812.VCC, Arduino_Nano.+5V, LED.pin3, 1N5818.cathode, RTCclock11.pin4
  N23: SK6812/WS2812.DIn, Arduino_Nano.D5, LED.pin2, RTCclock10.pin8
  N24: Arduino_Nano.TX, RTCclock10.pin1
  N25: Arduino_Nano.RX, RTCclock10.pin2
  N26: Arduino_Nano.RESET-3, RTCclock10.pin3
  N27: Arduino_Nano.D2, RTCclock10.pin5
  N28: Arduino_Nano.D3, RTCclock10.pin6
  N29: Arduino_Nano.D4, RTCclock10.pin7
  N30: Arduino_Nano.D6, RTCclock10.pin9
  N31: Arduino_Nano.D7, RTCclock10.pin10
  N32: Arduino_Nano.D8, RTCclock10.pin11
  N33: Arduino_Nano.D9, RTCclock10.pin12
  N34: Arduino_Nano.D10, RTCclock10.pin13
  N35: Arduino_Nano.D11, RTCclock10.pin14
  N36: Arduino_Nano.D12, RTCclock10.pin15
  N37: Arduino_Nano.D13, RTCclock11.pin15
  N38: Arduino_Nano.AREF, RTCclock11.pin13
  N39: Arduino_Nano.D14, RTCclock11.pin12
  N40: Arduino_Nano.D15, RTCclock11.pin11
  N41: Arduino_Nano.D16, RTCclock11.pin10, R16.Pin_1, LDR1.pin1
  N42: Arduino_Nano.D17, RTCclock11.pin9
  N43: Arduino_Nano.D20, RTCclock11.pin6
  N44: Arduino_Nano.D27, RTCclock11.pin5
  N45: Arduino_Nano.RESET-28, RTCclock11.pin3
  N46: Arduino_Nano.VIN, RTCclock11.pin1
  N47: RTC-0.pin5, SQW_32K-0.pin2
  N48: RTC-0.pin6, SQW_32K-0.pin1
  N49: RTC-1.pin5, SQW_32K-1.pin2
  N50: RTC-1.pin6, SQW_32K-1.pin1
  N51: RTC-2.pin5, SQW_32K-2.pin2
  N52: RTC-2.pin6, SQW_32K-2.pin1
  N53: RTC-3.pin5, SQW_32K-3.pin2
  N54: RTC-3.pin6, SQW_32K-3.pin1
  N55: RTC-4.pin5, SQW_32K-4.pin2
  N56: RTC-4.pin6, SQW_32K-4.pin1
  N57: RTC-5.pin5, SQW_32K-5.pin2
  N58: RTC-5.pin6, SQW_32K-5.pin1
  N59: RTC-6.pin5, SQW_32K6.pin2
  N60: RTC-6.pin6, SQW_32K6.pin1
  N61: RTC-7.pin5, SQW_32K7.pin2
  N62: RTC-7.pin6, SQW_32K7.pin1
  N63: POWER.pin2, 1N5818.anode, 1000_uF1.+

notes:
  Gnd Din 5V
  Gnd Dout 5V
  Gnd
  3V3
  SDA
  SCL
  SQW
  32K
  5V
  USB
  D5
  -
  +
  D7
  D2
  D3
  D4
  D12
  D11
  D10
  D9
  D8
  D6
  Rst
  RX
  TX
  D13
  A0
  A7
  A1
  Aref
  Vin
  A6
  A3
  A4
  A5
  A2

custom parts:
  Adafruit TCA9548A: You just found the perfect I2C sensor, and you want to wire up two or three or more of them to your Arduino when you realize "Uh oh, this chip has a fixed I2C address, and from what I know about I2C, you cannot have two devices with the same address on the same SDA/SCL pins!" Are you out of luck? You would be, if you didn't have this ultra-cool TCA9548A 1-to-8 I2C multiplexer! Finally, a way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
  SMD RGB LED (SK6812): The SK6812 is an RGB LED with a WS2811 control IC built right into the LED.
